# Fritzing sketch LED-pot (saved by Fritzing 0.9.9b)
breadboards: 1

parts:
  Part1 = Arduino Leonardo (Rev3b)
  LED1 = LED - 5mm [color="Red (633nm)" current=0.030 package="5 mm [THT]"]
  R1 = Resistor [tolerance=±5% power=0.25 resistance=220 package=THT]
  POT1 = Breadboard Trimpot

nets:
  N1: Part1.5V, R1.Pin_0, POT1.PIN1
  N2: Part1.GND, LED1.cathode, POT1.PIN3
  N3: Part1.A0, POT1.PIN2
  N4: LED1.anode, R1.Pin_1
